// Logisim project Projeto_FINAL.circ as structural Verilog: 3 circuits, main circuit Projeto_final
module ULA (
  input  \DIREÇÃO ,
  input  [3:0] in_2,
  input  [3:0] in_3,
  input  [2:0] in_4,
  output [3:0] SAIDA,
  output OVERFLOW,
  output ZERO
);

  wire adder_1_cout, and_1_out, and_2_out, decoder_1_out0, decoder_1_out1, decoder_1_out2, decoder_1_out3,
       decoder_1_out4, decoder_1_out5, decoder_1_out6, decoder_1_out7, not_2_out, subtractor_1_bout;
  wire [3:0] adder_1_out, controlled_buffer_6_out, not_1_out, or_2_out, shifter_1_out, shifter_2_out,
       subtractor_1_out;

  or or_1 (OVERFLOW, and_1_out, and_2_out);
  and and_1 (and_1_out, subtractor_1_bout, decoder_1_out2);
  and and_2 (and_2_out, adder_1_cout, decoder_1_out1);
  Decoder #(.select(3)) decoder_1 (
    .out0(decoder_1_out0), .out1(decoder_1_out1), .out2(decoder_1_out2), .out3(decoder_1_out3),
    .out4(decoder_1_out4), .out5(decoder_1_out5), .out6(decoder_1_out6), .out7(decoder_1_out7), .sel(in_4));  // open: en
  assign SAIDA = decoder_1_out0 ? in_3 : 4'bz;  // Controlled_Buffer controlled_buffer_1
  Adder #(.width(4)) adder_1 (.a(in_2), .b(in_3), .out(adder_1_out), .cout(adder_1_cout));  // open: cin
  assign SAIDA = decoder_1_out1 ? adder_1_out : 4'bz;  // Controlled_Buffer controlled_buffer_2
  Subtractor #(.width(4)) subtractor_1 (
    .a(in_2), .b(in_3), .out(subtractor_1_out), .bout(subtractor_1_bout));  // open: bin
  assign SAIDA = decoder_1_out2 ? subtractor_1_out : 4'bz;  // Controlled_Buffer controlled_buffer_3
  nor nor_1 (ZERO, decoder_1_out7, decoder_1_out6, SAIDA[3], SAIDA[2], SAIDA[1], SAIDA[0]);
  assign or_2_out = in_3 | in_2;  // OR_Gate or_2, 4 bits wide
  assign SAIDA = decoder_1_out3 ? or_2_out : 4'bz;  // Controlled_Buffer controlled_buffer_4
  assign not_1_out = ~in_3;  // NOT_Gate not_1, 4 bits wide
  assign SAIDA = decoder_1_out4 ? not_1_out : 4'bz;  // Controlled_Buffer controlled_buffer_5
  Shifter #(.width(4), .shift("lr")) shifter_1 (.in(in_2), .\dist (in_3[1:0]), .out(shifter_1_out));
  Shifter #(.width(4)) shifter_2 (.in(in_2), .\dist (in_3[1:0]), .out(shifter_2_out));
  assign controlled_buffer_6_out = \DIREÇÃO  ? shifter_1_out : 4'bz;  // Controlled_Buffer controlled_buffer_6
  assign controlled_buffer_6_out = not_2_out ? shifter_2_out : 4'bz;  // Controlled_Buffer controlled_buffer_7
  not not_2 (not_2_out, \DIREÇÃO );
  assign SAIDA = decoder_1_out5 ? controlled_buffer_6_out : 4'bz;  // Controlled_Buffer controlled_buffer_8
endmodule

module Projeto_final (
  input  Write___0____Read___1,
  input  \DIREÇAO ,
  output ZERO
);

  wire clock_1_out, not_1_out, not_2_out, REGISTRADOR_OVERFLOW_q, Reset_out, unidade_de_controle_1_clock_ac,
       unidade_de_controle_1_clock_ir, unidade_de_controle_1_clock_pc, unidade_de_controle_1_clock_ram,
       unidade_de_controle_1_load, \unidade_de_controle_1_módulo_de_endereçamento ,
       unidade_de_controle_1_reset_pc, ZERO_overflow, ZERO_zero;
  wire [2:0] unidade_de_controle_1_opcode;
  wire [3:0] multiplexer_1_out, ram_2_data, REGISTRADOR_AC_q, REGISTRADOR_PC_q,
       \unidade_de_controle_1_operando___saída_de_dados , ZERO_saida;
  wire [7:0] ram_1_data, REGISTRADOR_IR_q;

  Register #(.width(4)) REGISTRADOR_PC (
    .D(\unidade_de_controle_1_operando___saída_de_dados ), .en(not_1_out), .Q(REGISTRADOR_PC_q),
    .clk(unidade_de_controle_1_clock_pc), .clr(unidade_de_controle_1_reset_pc));
  not not_1 (not_1_out, unidade_de_controle_1_load);
  RAM #(.addrWidth(4)) ram_1 (.addr(REGISTRADOR_PC_q), .data(ram_1_data));  // open: sel, clk, ld, clr
  Clock clock_1 (.out(clock_1_out));
  Button Reset (.out(Reset_out));
  Register #(.trigger("falling")) REGISTRADOR_IR (
    .D(ram_1_data), .Q(REGISTRADOR_IR_q), .clk(unidade_de_controle_1_clock_ir));  // open: en, clr
  UNIDADE_DE_CONTROLE unidade_de_controle_1 (
    .\OPERANDO___saída_de_dados (\unidade_de_controle_1_operando___saída_de_dados ),
    .\MÓDULO_DE_ENDEREÇAMENTO (\unidade_de_controle_1_módulo_de_endereçamento ),
    .OPCODE(unidade_de_controle_1_opcode),
    .\INSTRUÇÃO___3___opcode___1___Mod_Endereçamento___4___Operando (REGISTRADOR_IR_q), .Clock(clock_1_out),
    .Reset(Reset_out), .Reset_PC(unidade_de_controle_1_reset_pc), .Clock_IR(unidade_de_controle_1_clock_ir),
    .Clock_PC(unidade_de_controle_1_clock_pc), .Clock_AC(unidade_de_controle_1_clock_ac),
    .Clock_RAM(unidade_de_controle_1_clock_ram), .ZERO(ZERO), .LOAD(unidade_de_controle_1_load),
    .OVERFLOW(REGISTRADOR_OVERFLOW_q));
  // Probe on REGISTRADOR_AC_q
  Multiplexer #(.width(4)) multiplexer_1 (
    .in0(\unidade_de_controle_1_operando___saída_de_dados ), .in1(ram_2_data), .out(multiplexer_1_out),
    .sel(\unidade_de_controle_1_módulo_de_endereçamento ));  // open: en
  ULA u_ZERO (
    .\DIREÇÃO (\DIREÇAO ), .in_2(REGISTRADOR_AC_q), .in_3(multiplexer_1_out), .ZERO(ZERO_zero),
    .OVERFLOW(ZERO_overflow), .in_4(unidade_de_controle_1_opcode), .SAIDA(ZERO_saida));
  // Probe on ZERO_saida
  Register #(.width(4)) REGISTRADOR_AC (
    .D(ZERO_saida), .Q(REGISTRADOR_AC_q), .clk(unidade_de_controle_1_clock_ac));  // open: en, clr
  RAM #(.addrWidth(4), .dataWidth(4)) ram_2 (
    .addr(\unidade_de_controle_1_operando___saída_de_dados ), .data(ram_2_data),
    .clk(unidade_de_controle_1_clock_ram), .ld(Write___0____Read___1));  // open: sel, clr
  not not_2 (not_2_out, Write___0____Read___1);
  // Probe on multiplexer_1_out
  // Probe on ram_2_data
  assign ram_2_data = not_2_out ? REGISTRADOR_AC_q : 4'bz;  // Controlled_Buffer controlled_buffer_1
  Register #(.width(1)) REGISTRADOR_OVERFLOW (
    .D(ZERO_overflow), .Q(REGISTRADOR_OVERFLOW_q), .clk(unidade_de_controle_1_clock_ac));  // open: en, clr
  Register #(.width(1)) REGISTRADOR_ZERO (
    .D(ZERO_zero), .Q(ZERO), .clk(unidade_de_controle_1_clock_ac));  // open: en, clr

  // Notes on the sheet:
  //   SAÍDA DE DADOS
endmodule

module UNIDADE_DE_CONTROLE (
  input  [7:0] \INSTRUÇÃO___3___opcode___1___Mod_Endereçamento___4___Operando ,
  input  Clock,
  input  Reset,
  input  OVERFLOW,
  input  ZERO,
  output Reset_PC,
  output Clock_IR,
  output Clock_PC,
  output Clock_AC,
  output Clock_RAM,
  output [3:0] \OPERANDO___saída_de_dados ,
  output \MÓDULO_DE_ENDEREÇAMENTO ,
  output [2:0] OPCODE,
  output LOAD
);

  wire and_1_out, and_3_out, and_7_out;
  wire [1:0] register_1_q;

  and and_1 (and_1_out, Clock_PC, \INSTRUÇÃO___3___opcode___1___Mod_Endereçamento___4___Operando [7], \INSTRUÇÃO___3___opcode___1___Mod_Endereçamento___4___Operando [6], \INSTRUÇÃO___3___opcode___1___Mod_Endereçamento___4___Operando [5], ~\INSTRUÇÃO___3___opcode___1___Mod_Endereçamento___4___Operando [4], OVERFLOW);  // AND_Gate
  Register #(.width(2)) register_1 (.Q(register_1_q), .clk(Clock), .clr(Reset));  // open: D, en
  and and_2 (Clock_IR, ~register_1_q[1], ~register_1_q[0]);  // AND_Gate
  and and_3 (and_3_out, Clock_PC, \INSTRUÇÃO___3___opcode___1___Mod_Endereçamento___4___Operando [7], ~\INSTRUÇÃO___3___opcode___1___Mod_Endereçamento___4___Operando [5], ~\INSTRUÇÃO___3___opcode___1___Mod_Endereçamento___4___Operando [4], ZERO);  // AND_Gate
  or or_1 (LOAD, and_1_out, and_3_out, and_7_out);
  and and_4 (Clock_PC, ~register_1_q[1], register_1_q[0]);  // AND_Gate
  and and_5 (Clock_RAM, register_1_q[1], register_1_q[0]);
  and and_6 (Clock_AC, register_1_q[1], ~register_1_q[0]);  // AND_Gate
  and and_7 (and_7_out, Clock_PC, \INSTRUÇÃO___3___opcode___1___Mod_Endereçamento___4___Operando [7], \INSTRUÇÃO___3___opcode___1___Mod_Endereçamento___4___Operando [6], \INSTRUÇÃO___3___opcode___1___Mod_Endereçamento___4___Operando [5], ~\INSTRUÇÃO___3___opcode___1___Mod_Endereçamento___4___Operando [4]);  // AND_Gate

  assign \MÓDULO_DE_ENDEREÇAMENTO  = \INSTRUÇÃO___3___opcode___1___Mod_Endereçamento___4___Operando [4];
  assign OPCODE = \INSTRUÇÃO___3___opcode___1___Mod_Endereçamento___4___Operando [7:5];
  assign \OPERANDO___saída_de_dados  = \INSTRUÇÃO___3___opcode___1___Mod_Endereçamento___4___Operando [3:0];
  assign Reset_PC = Reset;
endmodule
